# Fritzing sketch ESP8266-OLED-connections (saved by Fritzing 0.9.3b)

parts:
  OLED_I2C1 = OLED 128x64 I2C Monochrome Display
  Espessif_Serial_Wifi_Modul_1 = ESP8266 ESP01 [part_number=ESP8266 package=THT]

nets:
  N1: OLED_I2C1.SDA, Espessif_Serial_Wifi_Modul_1.GPIO00
  N2: OLED_I2C1.SCK, Espessif_Serial_Wifi_Modul_1.GPIO02
  VDD: OLED_I2C1.VDD, Espessif_Serial_Wifi_Modul_1.VCC
  GND: OLED_I2C1.GND, Espessif_Serial_Wifi_Modul_1.GND

custom parts:
  ESP8266 ESP01: Generic WiFi Module based on the ESP8266 with onboard PCB antenna and UART communications
